# Fritzing sketch Motor Shield (saved by Fritzing 0.9.2b)
breadboards: 1

parts:
  Part1 = Arduino Motor Shield (Rev3)
  J1 = Basic Servo
  J2 = Basic Servo
  V1 = DC Power [voltage=9V]
  RE1 = Rotary Encoder [package=THT]
  RE2 = Rotary Encoder [package=THT]

nets:
  N1: Part1.D8/BreakeB, Part1.D11_PWM/B, Part1.D13/DirB, J2.pulse
  N2: Part1.D9/BreakeA, Part1.D12/DirA, Part1.D3_PWM/A, J1.pulse
  N3: Part1.D4, RE2.EncoderPinB
  N4: Part1.D5_PWM, RE1.EncoderPinB
  N5: Part1.B-, J2.gnd
  N6: Part1.B+, J2.vcc
  N7: Part1.A-, J1.gnd
  N8: Part1.A+, J1.vcc
  GND: Part1.GND, RE1.EncoderPinC, RE2.EncoderPinC
  N9: Part1.5V, RE1.EncoderPinA, RE2.EncoderPinA
  N10: Part1.VIN, V1.V-
