# Fritzing sketch Whole System Diagram (saved by Fritzing 0.9.2b)
breadboards: 1

parts:
  Uno_with_Wifi_Shield = Arduino Uno (Rev3)
  Uno_with_Motor_Shield = Arduino Uno (Rev3)
  Uno_with_Sensor_Shield = Arduino Uno (Rev3)
  VCC1 = Battery block 9V
  R1 = Resistor [tolerance=±5% resistance=10k package=THT]
  R2 = Resistor [tolerance=±5% resistance=220 package=THT]

nets:
  N1: Uno_with_Wifi_Shield.A4/SDA, Uno_with_Motor_Shield.A4/SDA, Uno_with_Sensor_Shield.A4/SDA, R1.Pin_0
  N2: Uno_with_Wifi_Shield.A5/SCL, Uno_with_Motor_Shield.A5/SCL, Uno_with_Sensor_Shield.A5/SCL, R2.Pin_0
  5V: Uno_with_Wifi_Shield.5V, Uno_with_Motor_Shield.5V, Uno_with_Sensor_Shield.5V, R1.Pin_1, R2.Pin_1
  GND: Uno_with_Wifi_Shield.GND, Uno_with_Motor_Shield.GND, Uno_with_Sensor_Shield.GND, VCC1.-
  VIN: Uno_with_Wifi_Shield.VIN, Uno_with_Motor_Shield.VIN, Uno_with_Sensor_Shield.VIN, VCC1.+

notes:
  arduino with sensor shield
  arduino with wifi shield
  arduino with motor shield
